# Fritzing sketch Antenna Relay (saved by Fritzing 0.9.4)
perfboards: 1

parts:
  J1 = female pin header, 3 pins [form="♀ (female)"]
  ANTENNA = Antenna
  SMA_OUT = SMA Antenna Connector [package=sma-edge]
  U1 = RELAY [package=relay-t9a]
  Transistor = NPN-Transistor [package="TO92 [THT]"]
  part = Diode [package=diode-1n4001]
  R1 = Resistor [tolerance=±5% resistance=220 package=THT]

nets:
  N1: J1.pin1, R1.Pin_0
  N2: J1.pin2, U1.COIL2, part.A
  GND: J1.pin3, Transistor.E
  N3: ANTENNA.antenna_lead, SMA_OUT.SIGNAL
  N4: SMA_OUT.GND, U1.MAIN
  N5: U1.COIL1, Transistor.C, part.C
  Handheld Radio: U1.NC
  APRS: U1.NO
  N6: Transistor.B, R1.Pin_1

notes:
  Antenna Relay Board , Author: Alex Tate, 1
