# Fritzing sketch CutDown (saved by Fritzing 0.9.4)
perfboards: 1

parts:
  On_Board_Battery = Battery Holders [package=battery-aa]
  MOSFET = MOSFET-NCHANNEL [package=dpak]
  Nitinol_Coil = Inductor [package="400 mil [THT]"]
  R1 = Resistor [tolerance=±5% resistance=220 package=THT]
  J1 = female pin header, 2 pins [form="♀ (female)"]

nets:
  GND: On_Board_Battery.-, MOSFET.S, R1.Pin_0, J1.pin2
  N1: On_Board_Battery.+, Nitinol_Coil.pin_1
  N2: MOSFET.G, R1.Pin_1, J1.pin1
  N3: MOSFET.D, Nitinol_Coil.pin_0

notes:
  Balloon Wire Cut Down, Cut down for weather balloon project. Author: Alex Tate, 1
  Connector:
  - Left: Arduino IO (+)
  - Right: GND (-)
