# Fritzing sketch Integration Schematics (saved by Fritzing 0.9.4)
breadboards: 1

parts:
  Altimeter_Module_MS5607 = mystery part, 7 pins [chip_label=Altitude]
  SIM33EAU_GPS_Module = mystery part, 4 pins [chip_label=GPS]
  TNC = mystery part, 4 pins [chip_label=TNC]
  POWER_SOURCE = Battery
  Adafruit_MAX31865 = mystery part, 6 pins [chip_label=Temperature]
  OV5644_Camera_Module = IC, SIP package, 8 pins [chip_label=OV5642]
  ARDUINO_MEGA = Arduino Mega 2560 (Rev3)
  MicroSD_Module = Adafruit MicroSD card breakout board [part_number="Adafruit #254"]
  APRS = mystery part, 3 pins [chip_label=GPS]
  IC1 = Voltage Regulator [package=to-92]
  C1 = Ceramic Capacitor [capacitance=100nF package="100 mil [THT, multilayer]"]
  C2 = Ceramic Capacitor [capacitance=100nF package="100 mil [THT, multilayer]"]
  U1 = Chip antenna [part_number=Attenna package=antenna-chip4]  # not connected
  SJ2 = Solder Jumper [package=sj_2s-no]
  LED1 = LEDs [package=led10mm]
  MOSFET_Transistor = mystery part, 1 pin [chip_label="Wire cutter"]

nets:
  3.3V: Altimeter_Module_MS5607.pin1, TNC.pin1, ARDUINO_MEGA.3V3, MicroSD_Module.+3V3
  MISO: Altimeter_Module_MS5607.pin2, Altimeter_Module_MS5607.pin5, Altimeter_Module_MS5607.pin6, Adafruit_MAX31865.pin3, Adafruit_MAX31865.pin4, OV5644_Camera_Module.pin2, OV5644_Camera_Module.pin3, ARDUINO_MEGA.D48, MicroSD_Module.DO
  D24: Altimeter_Module_MS5607.pin3, ARDUINO_MEGA.D24
  SCL: Altimeter_Module_MS5607.pin4, Adafruit_MAX31865.pin2, ARDUINO_MEGA.D52, MicroSD_Module.CLK
  GND: Altimeter_Module_MS5607.pin7, SIM33EAU_GPS_Module.pin4, TNC.pin4, Adafruit_MAX31865.pin6, OV5644_Camera_Module.pin5, APRS.pin2, IC1.GND, C1.0, C2.0
  D14: SIM33EAU_GPS_Module.pin1, ARDUINO_MEGA.D14/TX3
  D15: SIM33EAU_GPS_Module.pin2, ARDUINO_MEGA.D15/RX3
  5V: SIM33EAU_GPS_Module.pin3, Adafruit_MAX31865.pin1, OV5644_Camera_Module.pin6, ARDUINO_MEGA.5V
  D18: TNC.pin2, ARDUINO_MEGA.D18/TX1
  D19: TNC.pin3, ARDUINO_MEGA.D19/RX1
  N1: POWER_SOURCE.+, SJ2.1
  D23: Adafruit_MAX31865.pin5, ARDUINO_MEGA.D23
  D25: OV5644_Camera_Module.pin1, ARDUINO_MEGA.D25
  SCK: OV5644_Camera_Module.pin4
  N2: OV5644_Camera_Module.pin7, ARDUINO_MEGA.D20/SDA, ARDUINO_MEGA.SDA
  N3: OV5644_Camera_Module.pin8, ARDUINO_MEGA.D21/SCL, ARDUINO_MEGA.SCL
  D10: ARDUINO_MEGA.D10_PWM, MOSFET_Transistor.pin1
  MOSA: ARDUINO_MEGA.D51
  D53: ARDUINO_MEGA.D53, MicroSD_Module.CS
  MOSI: MicroSD_Module.DI
  TX: APRS.pin1
  5VH: APRS.pin3, IC1.OUT, C1.1
  N4: IC1.IN, C2.1, SJ2.2, LED1.C, LED1.A

notes:
  VisonSat Tyriq Dominguez, 3

custom parts:
  Battery: Your standard 2x 18650 battery pack (7,4 Volts)
  Adafruit MicroSD card breakout board: Not just a simple breakout board, this microSD adapter goes the extra mile - designed for ease of use. Onboard 5v->3v regulator provides 150mA for power-hungry cards 3v level shifting means you can use this with ease on either 3v or 5v systems Uses a proper level shifting chip, not resistors: less problems, and faster read/write access Use 3 or 4 digital pins to read and write 2Gb+ of storage!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
