# Fritzing sketch wiring_diagram (saved by Fritzing 0.9.6b)
breadboards: 1

parts:
  part = mystery part, 1 pin [chip_label=5V part_number=VIN]
  part_2 = mystery part, 1 pin [chip_label=D50 part_number=MISO]
  part_3 = mystery part, 1 pin [chip_label=D52 part_number=SCK]
  part_4 = mystery part, 1 pin [chip_label=SDA part_number=SDA]
  part_5 = mystery part, 1 pin [chip_label="9 - 12V" part_number="BAT V+"]
  part_6 = mystery part, 1 pin [chip_label=GND part_number=GND]
  part_7 = mystery part, 1 pin [chip_label=D51 part_number=MOSI]
  part_8 = mystery part, 1 pin [chip_label=SCL(8) part_number=SCL]
  part_9 = mystery part, 1 pin [chip_label=D52 part_number=CLK]
  part_10 = mystery part, 1 pin [chip_label=D52 part_number=MISO]
  part_11 = mystery part, 1 pin [chip_label=5V part_number=VIN]
  part_12 = mystery part, 1 pin [chip_label=D51 part_number=MOSI]
  part_13 = mystery part, 1 pin [chip_label=GND part_number=GND]
  part_14 = mystery part, 1 pin [chip_label=GND part_number=GND]
  part_15 = mystery part, 1 pin [chip_label=D18 part_number=RX]
  part_16 = mystery part, 1 pin [chip_label=D19 part_number=TX]
  part_17 = mystery part, 1 pin [chip_label=D14 part_number=RXD]
  part_18 = mystery part, 1 pin [chip_label=D15 part_number=TXD]
  part_19 = mystery part, 1 pin [chip_label=5V part_number=VIN]
  part_20 = mystery part, 1 pin [chip_label=SDA part_number=SDA]
  part_21 = mystery part, 1 pin [chip_label=SCL part_number=SCL]
  part_22 = mystery part, 1 pin [chip_label=GND part_number=GND]
  part_23 = mystery part, 1 pin [chip_label=3.3V part_number=VIN]
  part_24 = mystery part, 1 pin [chip_label=3.3V part_number=VIN]
  part_25 = mystery part, 1 pin [chip_label=D51 part_number=DI]
  part_26 = mystery part, 1 pin [chip_label=GND part_number=GND]
  part_27 = mystery part, 1 pin [chip_label=D53 part_number=CS]
  part_28 = mystery part, 1 pin [chip_label=D50 part_number=DO]
  part_29 = mystery part, 1 pin [chip_label="TX ON GPS" part_number=RX]
  part_30 = mystery part, 1 pin [chip_label=3.3V part_number=VIN]
  part_31 = mystery part, 1 pin [chip_label=D7 part_number=CS]
  part_32 = mystery part, 1 pin [chip_label=GND part_number="BAT G"]
  part_33 = mystery part, 1 pin [chip_label=3.3V part_number=VIN]
  part_34 = mystery part, 1 pin [chip_label=GND part_number=GND]
  part_35 = mystery part, 1 pin [chip_label=SCL part_number=SCK]
  part_36 = mystery part, 1 pin [chip_label=SCL part_number=SCL]
  part_37 = female pin header, 1 pin [form="♀ (female)"]
  part_38 = female pin header, 1 pin [form="♀ (female)"]
  part_39 = female pin header, 1 pin [form="♀ (female)"]
  part_40 = female pin header, 1 pin [form="♀ (female)"]
  part_41 = female pin header, 1 pin [form="♀ (female)"]
  part_42 = female pin header, 1 pin [form="♀ (female)"]
  part_43 = female pin header, 1 pin [form="♀ (female)"]
  part_44 = female pin header, 1 pin [form="♀ (female)"]
  part_45 = female pin header, 1 pin [form="♀ (female)"]
  part_46 = female pin header, 1 pin [form="♀ (female)"]
  part_47 = female pin header, 1 pin [form="♀ (female)"]
  part_48 = female pin header, 1 pin [form="♀ (female)"]
  part_49 = female pin header, 1 pin [form="♀ (female)"]
  part_50 = female pin header, 1 pin [form="♀ (female)"]
  part_51 = female pin header, 1 pin [form="♀ (female)"]
  part_52 = female pin header, 1 pin [form="♀ (female)"]
  part_53 = female pin header, 1 pin [form="♀ (female)"]
  part_54 = female pin header, 1 pin [form="♀ (female)"]
  part_55 = female pin header, 1 pin [form="♀ (female)"]
  part_56 = female pin header, 1 pin [form="♀ (female)"]
  part_57 = female pin header, 1 pin [form="♀ (female)"]
  part_58 = female pin header, 1 pin [form="♀ (female)"]
  part_59 = female pin header, 1 pin [form="♀ (female)"]
  part_60 = female pin header, 1 pin [form="♀ (female)"]
  part_61 = female pin header, 1 pin [form="♀ (female)"]
  part_62 = female pin header, 1 pin [form="♀ (female)"]
  part_63 = female pin header, 1 pin [form="♀ (female)"]
  part_64 = female pin header, 1 pin [form="♀ (female)"]
  part_65 = female pin header, 1 pin [form="♀ (female)"]
  part_66 = female pin header, 1 pin [form="♀ (female)"]
  part_67 = female pin header, 1 pin [form="♀ (female)"]
  part_68 = female pin header, 1 pin [form="♀ (female)"]
  part_69 = female pin header, 1 pin [form="♀ (female)"]
  part_70 = female pin header, 1 pin [form="♀ (female)"]
  part_71 = female pin header, 1 pin [form="♀ (female)"]
  part_72 = female pin header, 1 pin [form="♀ (female)"]

nets:
  N1: part.pin1, part_37.pin1
  N2: part_2.pin1, part_38.pin1
  N3: part_3.pin1, part_39.pin1
  N4: part_4.pin1, part_40.pin1
  N5: part_5.pin1, part_41.pin1
  N6: part_6.pin1, part_43.pin1
  N7: part_7.pin1, part_42.pin1
  N8: part_8.pin1, part_44.pin1
  N9: part_9.pin1, part_69.pin1
  N10: part_10.pin1, part_47.pin1
  N11: part_11.pin1, part_48.pin1
  N12: part_12.pin1, part_70.pin1
  N13: part_13.pin1, part_71.pin1
  N14: part_14.pin1, part_59.pin1
  N15: part_15.pin1, part_60.pin1
  N16: part_16.pin1, part_57.pin1
  N17: part_17.pin1, part_56.pin1
  N18: part_18.pin1, part_55.pin1
  N19: part_19.pin1, part_50.pin1
  N20: part_20.pin1, part_63.pin1
  N21: part_21.pin1, part_64.pin1
  N22: part_22.pin1, part_61.pin1
  N23: part_23.pin1, part_62.pin1
  N24: part_24.pin1, part_52.pin1
  N25: part_25.pin1, part_68.pin1
  N26: part_26.pin1, part_51.pin1
  N27: part_27.pin1, part_65.pin1
  N28: part_28.pin1, part_66.pin1
  N29: part_29.pin1, part_53.pin1
  N30: part_30.pin1, part_54.pin1
  N31: part_31.pin1, part_46.pin1
  N32: part_32.pin1, part_45.pin1
  N33: part_33.pin1, part_58.pin1
  N34: part_34.pin1, part_49.pin1
  N35: part_35.pin1, part_67.pin1
  N36: part_36.pin1, part_72.pin1

notes:
  Camera
  Temp
  TNC
  GPS
  Altimeter
  SD
  APRS
  VisionSat20
