# Fritzing sketch TempSensor Schematic (saved by Fritzing 0.8.7b)
breadboards: 1

parts:
  Adafruit_Max31865 = Adafruit MAX31865 RTD Sensor Breakout
  Arduino_Uno = Arduino Uno (Rev3)

nets:
  VIN: Adafruit_Max31865.VIN, Arduino_Uno.5V
  GND: Adafruit_Max31865.GND, Arduino_Uno.GND
  N1: Adafruit_Max31865.SCLK, Arduino_Uno.D13/SCK
  N2: Adafruit_Max31865.SDO, Arduino_Uno.D12/MISO
  N3: Adafruit_Max31865.SDI, Arduino_Uno.D11_PWM/MOSI
  N4: Adafruit_Max31865.CS, Arduino_Uno.D10_PWM/SS

notes:
  RTDIN- to FORCE+ are already connected for our sensor
  The Max31865 Sensor allows for Hardware vs. Software SPI.
  For Hardware, the schematic below must be used exactly. While for Software, the CS pin on the sensor must be passed into D10 while other pins can be passed into whatever pins.

custom parts:
  Adafruit MAX31865 RTD Sensor Breakout: For precision temperature sensing, nothing beats a Platinum RTD. Resistance temperature detectors (RTDs) are temperature sensors that contain a resistor that changes resistance value as its temperature changes, basically a kind of thermistor. In this sensor, the resistor is actually a small strip of Platinum with a resistance of 100 ohms at 0°C, thus the name PT100. Compared to most NTC/PTC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
